// Logisim project Conversor Hexadecimal.circ as structural Verilog: 1 circuit, main circuit main
module main (
  input  _0,
  input  _1,
  input  _2,
  input  _3,
  input  _4,
  input  _5,
  input  _6,
  input  _7,
  input  _8,
  input  _9,
  input  A_ou_10,
  input  B_ou_11,
  input  C_ou_12,
  input  D_ou_13,
  input  E_ou_14,
  input  F_ou_15,
  output [3:0] \Tela_dos_Números 
);

  or or_1 (\Tela_dos_Números [3], _8, _9, A_ou_10, B_ou_11, C_ou_12, D_ou_13, E_ou_14, F_ou_15);
  or or_2 (\Tela_dos_Números [2], _4, _5, _6, _7, C_ou_12, D_ou_13, E_ou_14, F_ou_15);
  or or_3 (\Tela_dos_Números [1], _2, _3, _6, _7, A_ou_10, B_ou_11, E_ou_14, F_ou_15);
  or or_4 (\Tela_dos_Números [0], _1, _3, _5, _7, _9, B_ou_11, D_ou_13, F_ou_15);
endmodule
