// Logisim project Somador Completo.circ as structural Verilog: 1 circuit, main circuit main
module main (
  input  Te,
  input  A,
  input  B,
  output S,
  output Ts
);

  wire and_1_out, and_2_out, and_3_out, xor_1_out;

  xor xor_1 (xor_1_out, A, B);
  and and_1 (and_1_out, Te, A);
  and and_2 (and_2_out, Te, B);
  and and_3 (and_3_out, A, B);
  xor xor_2 (S, Te, xor_1_out);
  or or_1 (Ts, and_1_out, and_2_out, and_3_out);
endmodule
