// Logisim project UnidArit4bits.circ as structural Verilog: 1 circuit, main circuit main
module main (
  input  [3:0] in_1,
  input  [3:0] in_2,
  output [3:0] out_3,
  output out_4
);

  wire main_1_ts, main_2_ts, main_3_ts;

  Somador_Completo_main main_1 (.Te(1'b0), .A(in_1[0]), .B(in_2[0]), .S(out_3[0]), .Ts(main_1_ts));
  Somador_Completo_main main_2 (.Te(main_1_ts), .A(in_1[1]), .B(in_2[1]), .S(out_3[1]), .Ts(main_2_ts));
  Somador_Completo_main main_3 (.Te(main_2_ts), .A(in_1[2]), .B(in_2[2]), .S(out_3[2]), .Ts(main_3_ts));
  Somador_Completo_main main_4 (.Te(main_3_ts), .A(in_1[3]), .B(in_2[3]), .S(out_3[3]), .Ts(out_4));
endmodule
