// Logisim project Mux 2x1.circ as structural Verilog: 1 circuit, main circuit main
module main (
  input  A,
  input  a_2,
  input  b,
  output out_4
);

  wire and_1_out, and_2_out;

  and and_1 (and_1_out, ~A, a_2);  // AND_Gate
  and and_2 (and_2_out, A, b);
  or or_1 (out_4, and_1_out, and_2_out);
endmodule
