// Logisim project Mux-4bit.circ as structural Verilog: 1 circuit, main circuit main
module main (
  input  [3:0] in_1,
  input  [3:0] in_2,
  input  in_3,
  output [3:0] out_4
);

  Mux_2x1_main main_1 (.a_2(in_1[0]), .b(in_2[0]), .A(in_3), .out_4(out_4[0]));
  Mux_2x1_main main_2 (.a_2(in_1[1]), .b(in_2[1]), .A(in_3), .out_4(out_4[1]));
  Mux_2x1_main main_3 (.a_2(in_1[2]), .b(in_2[2]), .A(in_3), .out_4(out_4[2]));
  Mux_2x1_main main_4 (.a_2(in_1[3]), .b(in_2[3]), .A(in_3), .out_4(out_4[3]));
endmodule
