// Logisim project C2.circ as structural Verilog: 1 circuit, main circuit main
module main (
  input  [3:0] in_1,
  output [3:0] out_2
);

  wire main_1_ts, main_2_ts, main_3_ts, not_1_out, not_2_out, not_3_out, not_4_out;

  not not_1 (not_1_out, in_1[1]);
  not not_2 (not_2_out, in_1[2]);
  not not_3 (not_3_out, in_1[3]);
  not not_4 (not_4_out, in_1[0]);
  Somador_Completo_main main_1 (.Te(1'b0), .A(not_4_out), .B(1'b1), .S(out_2[0]), .Ts(main_1_ts));
  Somador_Completo_main main_2 (.Te(main_1_ts), .A(not_1_out), .B(1'b0), .S(out_2[1]), .Ts(main_2_ts));
  Somador_Completo_main main_3 (.Te(main_2_ts), .A(not_2_out), .B(1'b0), .S(out_2[2]), .Ts(main_3_ts));
  Somador_Completo_main main_4 (.Te(main_3_ts), .A(not_3_out), .B(1'b0), .S(out_2[3]));  // open: Ts
endmodule
