// Logisim project Calculadora Hexadecimal.circ as structural Verilog: 1 circuit, main circuit main
module main (
  input  _0,
  input  _1,
  input  _2,
  input  _3,
  input  _4,
  input  _5,
  input  _6,
  input  _7,
  input  _8,
  input  _9,
  input  _10,
  input  _11,
  input  _12,
  input  _13,
  input  _14,
  input  _15,
  input  _0_2,
  input  _1_2,
  input  _2_2,
  input  _3_2,
  input  _4_2,
  input  _5_2,
  input  _6_2,
  input  _7_2,
  input  _8_2,
  input  _9_2,
  input  _10_2,
  input  _11_2,
  input  _12_2,
  input  \Subtração ,
  input  _13_2,
  input  _14_2,
  input  _15_2
);

  wire and_1_out, main_5_out_4, main_6_a, main_6_b, main_6_c, main_6_d, main_6_e, main_6_f, main_6_g;
  wire [3:0] \main_1_tela_dos_números , \main_2_tela_dos_números , main_3_out_2, main_4_out_4, main_5_out_3;

  Conversor_Hexadecimal_main main_1 (
    ._0(_0), ._1(_1), ._2(_2), ._3(_3), ._4(_4), ._5(_5), ._6(_6), ._7(_7), ._8(_8), ._9(_9), .A_ou_10(_10),
    .B_ou_11(_11), .C_ou_12(_12), .D_ou_13(_13), .E_ou_14(_14), .F_ou_15(_15),
    .\Tela_dos_Números (\main_1_tela_dos_números ));
  Conversor_Hexadecimal_main main_2 (
    ._0(_0_2), ._1(_1_2), ._2(_2_2), ._3(_3_2), ._4(_4_2), ._5(_5_2), ._6(_6_2), ._7(_7_2), ._8(_8_2),
    ._9(_9_2), .A_ou_10(_10_2), .B_ou_11(_11_2), .C_ou_12(_12_2), .D_ou_13(_13_2), .E_ou_14(_14_2),
    .F_ou_15(_15_2), .\Tela_dos_Números (\main_2_tela_dos_números ));
  C2_main main_3 (.in_1(\main_2_tela_dos_números ), .out_2(main_3_out_2));
  Mux_4bit_main main_4 (
    .in_1(\main_2_tela_dos_números ), .in_2(main_3_out_2), .in_3(\Subtração ), .out_4(main_4_out_4));
  UnidArit4bits_main main_5 (
    .in_1(\main_1_tela_dos_números ), .in_2(main_4_out_4), .out_4(main_5_out_4), .out_3(main_5_out_3));
  and and_1 (and_1_out, main_5_out_4, ~\Subtração );  // AND_Gate
  _7_seg_main main_6 (
    .in_1(main_5_out_3), .a(main_6_a), .b(main_6_b), .c(main_6_c), .d(main_6_d), .e(main_6_e), .f(main_6_f),
    .g(main_6_g));
  _7_Segment_Display u_7_segment_display_1 (.b(and_1_out), .c(and_1_out));  // open: g, f, a, e, d, dp
  _7_Segment_Display u_7_segment_display_2 (
    .g(main_6_g), .f(main_6_f), .a(main_6_a), .b(main_6_b), .e(main_6_e), .d(main_6_d), .c(main_6_c));  // open: dp
endmodule
